# Fritzing sketch eletrica (saved by Fritzing 0.9.3b)
breadboards: 1

parts:
  Componente1 = Arduino Mega 2560 (Rev3)
  J3 = Basic Servo
  M1 = DC Motor
  M2 = DC Motor
  S1 = H-Bridge with L298N
  U1 = LM2596 step down module
  Componente2 = SRF05 Ultrasonic Rangefinder
  D1 = Diode [package=diode-1n4001]
  J2 = Basic Servo
  J1 = Basic Servo
  J4 = Power Jack [package=power_jack_pth_lock]
  Componente3 = Bluetooth HC-05 Macho  # not connected
  R1 = Resistor [tolerance=±5% resistance=220 package="1206 [SMD]"]
  R2 = Resistor [tolerance=±5% resistance=220 package="2512 [SMD]"]

nets:
  N1: Componente1.D18/TX1, R2.Pin_0
  N2: Componente1.D8_PWM, D1.C
  N3: Componente1.D2_PWM, J1.pulse
  N4: Componente1.D3_PWM, J2.pulse
  N5: Componente1.D4_PWM, J3.pulse
  N6: Componente1.D22, Componente2.Trig
  N7: Componente1.D23, Componente2.Echo
  GND: J3.gnd, U1.IN-, U1.OUT-, J4.GND
  VCC: J3.vcc, U1.OUT+, J1.vcc
  N8: M1.pin_1, S1.M2-02
  N9: M1.pin_2, S1.M2-01
  N10: M2.pin_1, S1.M1-02
  N11: M2.pin_2, S1.M1-01
  N12: U1.IN+, J4.PWR
  N13: Componente2.GND, D1.A, R1.Pin_0
  N14: R1.Pin_1, R2.Pin_1

custom parts:
  H-Bridge with L298N: h-bridge
  LM2596 step down module: LM2596 DC-DC step down power supply module 3 A.
